# Fritzing sketch 12864 SPI (saved by Fritzing 0.9.3b)
perfboards: 1

parts:
  U1 = Graphical LCD 128x64 [package=lcd-g12864]
  U2 = POT [package=3362u]
  R1 = Resistor [tolerance=±1% resistance=47 package="0402 [SMD]"]

nets:
  N1: U1.VDD, U1.K, U2.E
  N2: U1.VSS, R1.Pin_0
  N3: U1.VEE, U2.S
  N4: U1.A, U2.A
