# Fritzing sketch Atmega328P board (saved by Fritzing 0.9.3b)
perfboards: 1

parts:
  U1 = atmega328 [package=dip]
  XTAL1 = Crystal [frequency="16 Mhz" package=SMD]
  C1 = Capacitor [part_number=22 package=cap-pth-small2]
  S1 = Pushbutton [package=THT]
  R1 = Resistor [tolerance=±0.1% resistance=10k package="2512 [SMD]"]
  C2 = Capacitor [part_number=22 package=cap-pth-small2]

nets:
  N1: U1.RESET, S1.leg0, R1.Pin_1
  N2: U1.XLAT1, XTAL1.pin_0, C2.2
  N3: U1.XLAT2, XTAL1.pin_1, C1.1
  N4: U1.AVCC, U1.AREF
  N5: C1.2, C2.1
