# Fritzing sketch Final (saved by Fritzing 0.9.3b)
perfboards: 10

parts:
  U4 = LM2596-Step-Down-Converter [package=THT]
  U5 = LM2596-Step-Down-Converter [package=THT]
  J3 = Power Jack [package=power_jack_smd]
  S2 = Toggle Switch [package=THT]
  LED2 = LEDs [package=led10mm]
  LCD3 = LCD screen
  C5 = Capacitor [part_number=22 package=cap-pth-small2]
  XTAL3 = Crystal [frequency="16 Mhz" package=SMD]
  S13 = Pushbutton [package="[THT]"]
  S14 = Pushbutton [package="[THT]"]
  U6 = atmega328 [package=dip]
  LCM1602_IIC3 = LCM1602 IIC [part_number="LCM1602 IIC" chip_label="LCM1602 IIC" package="DIP (Dual Inline) [THT]"]
  S15 = Pushbutton [package=THT]
  S16 = Pushbutton [package="[THT]"]
  R4 = Resistor [tolerance=±0.1% resistance=10k package="2512 [SMD]"]
  S17 = Pushbutton [package="[THT]"]
  C6 = Capacitor [part_number=22 package=cap-pth-small2]
  S18 = Round Pushbutton
  S19 = Round Pushbutton
  U7 = Graphical LCD 128x64 [package=lcd-g12864]
  U8 = POT [package=3362u]
  R5 = Resistor [tolerance=±1% resistance=47 package="0402 [SMD]"]
  C7 = Capacitor [part_number=22 package=cap-pth-small2]
  XTAL4 = Crystal [frequency="16 Mhz" package=SMD]
  U9 = atmega328 [package=dip]
  S20 = Pushbutton [package=THT]
  R6 = Resistor [tolerance=±0.1% resistance=10k package="2512 [SMD]"]
  C8 = Capacitor [part_number=22 package=cap-pth-small2]
  M16 = DC Motor
  M17 = DC Motor
  M18 = DC Motor
  M19 = DC Motor
  M20 = DC Motor
  Q14 = Basic FET N-Channel [package="TO220 [THT]"]
  Q15 = Basic FET N-Channel [package="TO220 [THT]"]
  Q16 = Basic FET N-Channel [package="TO220 [THT]"]
  Q17 = Basic FET N-Channel [package="TO220 [THT]"]
  Q18 = Basic FET N-Channel [package="TO220 [THT]"]
  RGB_Strip_LED4 = RGB Strip LED
  Q19 = Basic FET N-Channel [package="D2Pak [SMD]"]
  Q20 = Basic FET N-Channel [package="D2Pak [SMD]"]
  Q21 = Basic FET N-Channel [package="D2Pak [SMD]"]
  IC1 = 24LC128 [package=THT]

nets:
  N1: U4.pin1, S2.COM, LED2.A
  N2: U4.pin2, J3.GND, LED2.C
  N3: U4.pin4, U5.pin4
  N4: U5.pin3, R6.Pin_0
  N5: J3.GNDBREAK, S2.L1
  VSS: LCD3.VSS, LCM1602_IIC3.VSS
  VDD: LCD3.VDD, LCM1602_IIC3.VDD
  N6: LCD3.V0, LCM1602_IIC3.V0
  N7: LCD3.RS, LCM1602_IIC3.RS
  N8: LCD3.R/W, LCM1602_IIC3.RW
  N9: LCD3.E, LCM1602_IIC3.E
  N10: LCD3.DB0, LCM1602_IIC3.D0
  N11: LCD3.DB1, LCM1602_IIC3.D1
  N12: LCD3.DB2, LCM1602_IIC3.D2
  N13: LCD3.DB3, LCM1602_IIC3.D3
  N14: LCD3.DB4, LCM1602_IIC3.D4
  N15: LCD3.DB5, LCM1602_IIC3.D5
  N16: LCD3.DB6, LCM1602_IIC3.D6
  N17: LCD3.DB7, LCM1602_IIC3.D7
  N18: LCD3.LED+, LCM1602_IIC3.A
  N19: LCD3.LED-, LCM1602_IIC3.K
  N20: C5.1, XTAL3.pin_1, U6.XLAT2
  N21: C5.2, C6.1
  N22: XTAL3.pin_0, U6.XLAT1, C6.2
  N23: S13.Pin_1, S13.Pin_2, U6.D13
  N24: S13.Pin_3, S13.Pin_4, S14.Pin_1, S14.Pin_2, S16.Pin_3, S16.Pin_4, S17.Pin_3, S17.Pin_4, S18.leg0, S19.leg1
  N25: S14.Pin_3, S14.Pin_4, U6.D12
  N26: U6.RESET, S15.leg0, R4.Pin_1
  N27: U6.D5_(PWM), U7.E
  N28: U6.D6_(PWM), U7.D_I
  N29: U6.D7, U7.R_W
  N30: U6.D8, S18.leg1
  N31: U6.D9_(PWM), S19.leg0
  N32: U6.D10_(PWM), S16.Pin_1, S16.Pin_2
  N33: U6.D11_(PWM), S17.Pin_1, S17.Pin_2
  N34: U6.AVCC, U6.AREF
  N35: U6.GND#21, LCM1602_IIC3.GND, S15.leg1, Q14.source, Q18.source
  N36: U6.A4, LCM1602_IIC3.SDA
  N37: U6.A5, LCM1602_IIC3.SCL
  N38: LCM1602_IIC3.LED_A, LCM1602_IIC3.LED_B
  N39: R4.Pin_0, U9.AVCC, U9.AREF
  N40: U7.VDD, U7.K, U8.E
  N41: U7.VSS, R5.Pin_0
  N42: U7.VEE, U8.S
  N43: U7.A, U8.A
  N44: C7.1, XTAL4.pin_1, U9.XLAT2
  N45: C7.2, C8.1
  N46: XTAL4.pin_0, U9.XLAT1, C8.2
  N47: U9.RESET, S20.leg0, R6.Pin_1
  N48: U9.D4, Q14.gate
  N49: U9.D5_(PWM), Q17.gate
  N50: U9.D6_(PWM), Q15.gate
  N51: U9.D7, Q16.gate
  N52: U9.D8, Q18.gate
  N53: U9.D9_(PWM), Q20.Gate
  N54: U9.D10_(PWM), Q19.Gate
  N55: U9.D11_(PWM), Q21.Gate
  N56: U9.A4, IC1.SDA_-_I2C_Data
  N57: U9.A5, IC1.SCL_-_I2C_Clock
  N58: S20.leg1, Q21.source
  N59: M16.pin_1, Q16.drain
  N60: M16.pin_2, M17.pin_2, M18.pin_2, M19.pin_2, M20.pin_2
  N61: M17.pin_1, Q14.drain
  N62: M18.pin_1, Q18.drain
  N63: M19.pin_1, Q17.drain
  N64: M20.pin_1, Q15.drain
  N65: RGB_Strip_LED4.Green_Connect, Q21.drain
  N66: RGB_Strip_LED4.Red_Connect, Q19.drain
  N67: RGB_Strip_LED4.Blue_Connect, Q20.drain
  N68: Q19.source, Q20.source
  N69: IC1.A0, IC1.0V

custom parts:
  LM2596-Step-Down-Converter: A dummy, proxy, ersatz, stand-in part for whatever you want. With 4 pins on a 100 mil inline pin header footprint.
  LCM1602 IIC: I2C-Module to use a 1602 or 2004 LCD on with the wire.h libory Serial LCD Modul
  RGB Strip LED: A tri-color Strip LED with red, green and blue. Based on LED SMD 5050 RGB Pin order: common cathode - green - red - blue
