# Fritzing sketch LED Strip (saved by Fritzing 0.9.3b)
perfboards: 1

parts:
  RGB_Strip_LED2 = RGB Strip LED
  Q1 = Basic FET N-Channel [package="D2Pak [SMD]"]
  Q2 = Basic FET N-Channel [package="D2Pak [SMD]"]
  Q3 = Basic FET N-Channel [package="D2Pak [SMD]"]

nets:
  N1: RGB_Strip_LED2.Green_Connect, Q1.drain
  N2: RGB_Strip_LED2.Red_Connect, Q3.drain
  N3: RGB_Strip_LED2.Blue_Connect, Q2.drain
  N4: Q2.source, Q3.source

custom parts:
  RGB Strip LED: A tri-color Strip LED with red, green and blue. Based on LED SMD 5050 RGB Pin order: common cathode - green - red - blue
