# Fritzing sketch Master (saved by Fritzing 0.9.3b)
perfboards: 4

parts:
  U2 = atmega328 [package=dip]
  S2 = Pushbutton [package=THT]
  XTAL2 = Crystal [frequency="16 Mhz" package=SMD]
  C3 = Capacitor [part_number=22 package=cap-pth-small2]
  C4 = Capacitor [part_number=22 package=cap-pth-small2]
  R2 = Resistor [tolerance=±0.1% resistance=10k package="2512 [SMD]"]
  LCD2 = LCD screen
  LCM1602_IIC2 = LCM1602 IIC [part_number="LCM1602 IIC" chip_label="LCM1602 IIC" package="DIP (Dual Inline) [THT]"]
  S7 = Pushbutton [package="[THT]"]
  S8 = Pushbutton [package="[THT]"]
  S9 = Pushbutton [package="[THT]"]
  S10 = Pushbutton [package="[THT]"]
  S11 = Round Pushbutton
  S12 = Round Pushbutton
  U3 = Graphical LCD 128x64 [package=lcd-g12864]
  U4 = POT [package=3362u]
  R3 = Resistor [tolerance=±1% resistance=47 package="0402 [SMD]"]

nets:
  N1: U2.RESET, S2.leg0, R2.Pin_1
  N2: U2.XLAT1, XTAL2.pin_0, C4.2
  N3: U2.XLAT2, XTAL2.pin_1, C3.1
  N4: U2.D5_(PWM), U3.E
  N5: U2.D6_(PWM), U3.D_I
  N6: U2.D7, U3.R_W
  N7: U2.D8, S11.leg1
  N8: U2.D9_(PWM), S12.leg0
  N9: U2.D10_(PWM), S9.Pin_1, S9.Pin_2
  N10: U2.D11_(PWM), S10.Pin_1, S10.Pin_2
  N11: U2.D12, S8.Pin_3, S8.Pin_4
  N12: U2.D13, S7.Pin_1, S7.Pin_2
  N13: U2.AVCC, U2.AREF
  N14: U2.GND#21, S2.leg1, LCM1602_IIC2.GND
  N15: U2.A4, LCM1602_IIC2.SDA
  N16: U2.A5, LCM1602_IIC2.SCL
  N17: C3.2, C4.1
  VSS: LCD2.VSS, LCM1602_IIC2.VSS
  VDD: LCD2.VDD, LCM1602_IIC2.VDD
  N18: LCD2.V0, LCM1602_IIC2.V0
  N19: LCD2.RS, LCM1602_IIC2.RS
  N20: LCD2.R/W, LCM1602_IIC2.RW
  N21: LCD2.E, LCM1602_IIC2.E
  N22: LCD2.DB0, LCM1602_IIC2.D0
  N23: LCD2.DB1, LCM1602_IIC2.D1
  N24: LCD2.DB2, LCM1602_IIC2.D2
  N25: LCD2.DB3, LCM1602_IIC2.D3
  N26: LCD2.DB4, LCM1602_IIC2.D4
  N27: LCD2.DB5, LCM1602_IIC2.D5
  N28: LCD2.DB6, LCM1602_IIC2.D6
  N29: LCD2.DB7, LCM1602_IIC2.D7
  N30: LCD2.LED+, LCM1602_IIC2.A
  N31: LCD2.LED-, LCM1602_IIC2.K
  N32: LCM1602_IIC2.LED_A, LCM1602_IIC2.LED_B
  N33: S7.Pin_3, S7.Pin_4, S8.Pin_1, S8.Pin_2, S9.Pin_3, S9.Pin_4, S10.Pin_3, S10.Pin_4, S11.leg0, S12.leg1
  N34: U3.VDD, U3.K, U4.E
  N35: U3.VSS, R3.Pin_0
  N36: U3.VEE, U4.S
  N37: U3.A, U4.A

custom parts:
  LCM1602 IIC: I2C-Module to use a 1602 or 2004 LCD on with the wire.h libory Serial LCD Modul
