# Fritzing sketch Peristaltic pump (saved by Fritzing 0.9.3b)
perfboards: 2

parts:
  M8 = DC Motor
  Q1 = Basic FET N-Channel [package="TO220 [THT]"]
  Q2 = Basic FET N-Channel [package="TO220 [THT]"]
  Q3 = Basic FET N-Channel [package="TO220 [THT]"]
  Q4 = Basic FET N-Channel [package="TO220 [THT]"]
  Q5 = Basic FET N-Channel [package="TO220 [THT]"]
  M6 = DC Motor
  M10 = DC Motor
  M7 = DC Motor
  M9 = DC Motor

nets:
  N1: M8.pin_1, Q5.drain
  N2: M8.pin_2, M6.pin_2, M10.pin_2, M7.pin_2, M9.pin_2
  N3: Q1.drain, M7.pin_1
  N4: Q2.drain, M9.pin_1
  N5: Q3.drain, M10.pin_1
  N6: Q4.drain, M6.pin_1
