# Fritzing sketch Power (saved by Fritzing 0.9.3b)
perfboards: 1

parts:
  J2 = Power Jack [package=power_jack_smd]
  S1 = Toggle Switch [package=THT]
  U2 = LM2596-Step-Down-Converter [package=THT]
  U3 = LM2596-Step-Down-Converter [package=THT]
  LED1 = LEDs [package=led10mm]

nets:
  N1: J2.GND, U2.pin2, LED1.C
  N2: J2.GNDBREAK, S1.L1
  N3: S1.COM, U2.pin1, LED1.A
  N4: U2.pin4, U3.pin4

custom parts:
  LM2596-Step-Down-Converter: A dummy, proxy, ersatz, stand-in part for whatever you want. With 4 pins on a 100 mil inline pin header footprint.
