# Fritzing sketch Slave (saved by Fritzing 0.9.3b)
perfboards: 4

parts:
  C3 = Capacitor [part_number=22 package=cap-pth-small2]
  XTAL2 = Crystal [frequency="16 Mhz" package=SMD]
  U2 = atmega328 [package=dip]
  S2 = Pushbutton [package=THT]
  R2 = Resistor [tolerance=±0.1% resistance=10k package="2512 [SMD]"]
  C4 = Capacitor [part_number=22 package=cap-pth-small2]
  M11 = DC Motor
  M12 = DC Motor
  M13 = DC Motor
  M14 = DC Motor
  M15 = DC Motor
  Q6 = Basic FET N-Channel [package="TO220 [THT]"]
  Q7 = Basic FET N-Channel [package="TO220 [THT]"]
  Q8 = Basic FET N-Channel [package="TO220 [THT]"]
  Q9 = Basic FET N-Channel [package="TO220 [THT]"]
  Q10 = Basic FET N-Channel [package="TO220 [THT]"]
  RGB_Strip_LED3 = RGB Strip LED
  Q11 = Basic FET N-Channel [package="D2Pak [SMD]"]
  Q12 = Basic FET N-Channel [package="D2Pak [SMD]"]
  Q13 = Basic FET N-Channel [package="D2Pak [SMD]"]

nets:
  N1: C3.1, XTAL2.pin_1, U2.XLAT2
  N2: C3.2, C4.1
  N3: XTAL2.pin_0, U2.XLAT1, C4.2
  N4: U2.RESET, S2.leg0, R2.Pin_1
  N5: U2.D4, Q10.gate
  N6: U2.D5_(PWM), Q7.gate
  N7: U2.D6_(PWM), Q9.gate
  N8: U2.D7, Q8.gate
  N9: U2.D8, Q6.gate
  N10: U2.D9_(PWM), Q12.Gate
  N11: U2.D10_(PWM), Q11.Gate
  N12: U2.D11_(PWM), Q13.Gate
  N13: U2.AVCC, U2.AREF
  N14: M11.pin_1, Q8.drain
  N15: M11.pin_2, M12.pin_2, M13.pin_2, M14.pin_2, M15.pin_2
  N16: M12.pin_1, Q10.drain
  N17: M13.pin_1, Q6.drain
  N18: M14.pin_1, Q7.drain
  N19: M15.pin_1, Q9.drain
  N20: Q6.source, Q10.source
  N21: RGB_Strip_LED3.Green_Connect, Q13.drain
  N22: RGB_Strip_LED3.Red_Connect, Q11.drain
  N23: RGB_Strip_LED3.Blue_Connect, Q12.drain
  N24: Q11.source, Q12.source

custom parts:
  RGB Strip LED: A tri-color Strip LED with red, green and blue. Based on LED SMD 5050 RGB Pin order: common cathode - green - red - blue
