# Fritzing sketch buttons (saved by Fritzing 0.9.3b)
perfboards: 2

parts:
  S1 = Pushbutton [package="[THT]"]
  S2 = Pushbutton [package="[THT]"]
  S3 = Pushbutton [package="[THT]"]
  S4 = Pushbutton [package="[THT]"]
  S5 = Round Pushbutton
  S6 = Round Pushbutton

nets:
  N1: S1.Pin_1, S1.Pin_2
  N2: S1.Pin_3, S1.Pin_4, S2.Pin_1, S2.Pin_2, S3.Pin_3, S3.Pin_4, S4.Pin_3, S4.Pin_4, S5.leg0, S6.leg1
  N3: S2.Pin_3, S2.Pin_4
  N4: S3.Pin_1, S3.Pin_2
  N5: S4.Pin_1, S4.Pin_2
